# Fritzing sketch lasertag (saved by Fritzing 1.0.0rc)
breadboards: 1

parts:
  Grove1 = Grove OLED 128x96  # not connected
  IC1 = ULN2003A [package="DIP16 [THT]"]
  J1 = Piezo Speaker
  IR1 = TSOP312.., 314.. [package=THT]
  LED1 = LEDs [package=led10mm]
  Mod1 = Amica NodeMCU DEVKIT 1.0
  S1 = SWITCH-MOMENTARY-2 [package=tactile-pth-12mm]
  R1 = Resistor [tolerance=±5% power=0.25W resistance=220 package=THT]
  LED2 = smd LED [color="Red (633nm)" package="1206 [SMD]"]
  LED3 = smd LED [color="Blue (525nm)" package="1206 [SMD]"]

nets:
  N1: IC1.In_2, LED2.cathode
  N2: IC1.In_5, LED3.cathode
  N3: IC1.In_6, J1.pin1
  N4: IC1.In_7, LED1.C
  N5: IC1.COM_-_Common, IR1.GND, R1.Pin_1
  N6: IC1.Out_7, Mod1.pin7
  N7: IC1.Out_6, Mod1.pin6
  N8: IC1.Out_5, Mod1.pin8
  N9: IC1.Out_2, Mod1.pin_15
  N10: J1.pin2, LED1.A, LED2.anode
  N11: IR1.Vs, Mod1.pin_12
  N12: Mod1.pin1, Mod1.pin_10, Mod1.pin_26
  N13: Mod1.pin2, Mod1.pin_9, Mod1.pin_25, Mod1.pin_29
  N14: Mod1.pin_11, S1.2, R1.Pin_0
